// Logisim project Arch-242-B.circ as structural Verilog
module main (
);

  wire ACCWrite, ALUSrcA, ALUSrcB, Branch, Branch_result, CF, CF_ALUResult, CFWrite, clk, clock_1_out,
       ConcatSrc, Is1byte, Is2byte, Is2ndbyte, IsSupported, Jump, MemWrite, Power, RegWrite, TEMPWrite, Zero;
  wire [1:0] PCTargetControl, ResultSrc;
  wire [1:1] PCSrc;
  wire [2:0] ImmSrc, rd_t, rs;
  wire [3:0] ACCData, CFControl, RD, SrcA;
  wire [4:0] ALUControl;
  wire [7:0] ALUResult, ImmExt, Instr, multiplexer_4_out, Prev_byte, RBRA, RDRC, ReadData, SrcB;
  wire [15:0] ImmExt16, PC, PCNext, PCPlus8, PCPlus16, PCTarget, Result, TEMP, TEMPWD;

  // Probe on PCNext
  Clock clock_1 (.out(clock_1_out));
  // Probe on {PCSrc[1], 1'b0}
  Register #(.width(1)) register_1 (.D(Is2byte), .clk(clk), .Q(Is2ndbyte));  // open: en, clr
  Register register_2 (.D(Instr), .clk(clk), .Q(Prev_byte));  // open: en, clr
  Register #(.width(1)) register_3 (.D(ALUResult[0]), .clk(clk), .Q(Branch_result));  // open: en, clr
  Register #(.width(16)) u_PC (.D(PCNext), .clk(clk), .Q(PC));  // open: en, clr
  and and_1 (clk, clock_1_out, Power);
  // Probe on PCNext
  Multiplexer #(.enable("true"), .select(2), .width(16)) multiplexer_1 (
    .in0(PCPlus8), .in1(PCPlus16), .in2(PCTarget), .out(PCNext), .sel({PCSrc[1], 1'b0}));  // open: in3, en
  // Probe on PC
  // Probe on PC
  // Probe on PCPlus8
  Adder #(.width(16)) adder_1 (.a(PC), .b(16'h1), .out(PCPlus8));  // open: cin, cout
  // Probe on PCPlus16
  Adder #(.width(16)) adder_2 (.a(PC), .b(16'h2), .out(PCPlus16));  // open: cin, cout
  LED led_1 (.in(IsSupported));
  instmem instmem_1 (.Address(PC), .Instr(Instr));
  // Probe on Instr
  // Probe on Instr
  // Probe on Instr
  // Probe on ImmSrc
  maindecoder maindecoder_1 (
    .Inst(Instr), .Is2ndbyte(Is2ndbyte), .Prev_byte(Prev_byte), .Branch_result(Branch_result),
    .IsSupported(IsSupported), .Branch(Branch), .ResultSrc(ResultSrc), .MemWrite(MemWrite),
    .ALUSrcA(ALUSrcA), .ImmSrc(ImmSrc), .RegWrite(RegWrite), .Jump(Jump), .CFWrite(CFWrite),
    .TEMPWrite(TEMPWrite), .Is1byte(Is1byte), .Is2byte(Is2byte), .CFControl(CFControl),
    .ALUControl(ALUControl), .ALUSrcB(ALUSrcB), .ACCWrite(ACCWrite), .ConcatSrc(ConcatSrc), .rs(rs),
    .rd(rd_t), .PCTargetControl(PCTargetControl), .Power(Power));
  regfile regfile_1 (
    .A3(rd_t), .WD3(ALUResult), .TEMPIn(TEMPWD), .CFIn(CF_ALUResult), .A1(rs), .TEMPWrite(TEMPWrite),
    .CFWrite(CFWrite), .ACCWrite(ACCWrite), .ACCIn(ALUResult), .CLK(clk), .WE3(RegWrite), .RDOut(RD),
    .ACCOut(ACCData), .CFOut(CF), .TEMPOut(TEMP), .RBRAOut(RBRA), .RDRCOut(RDRC));  // open: Reset
  extender extender_1 (.Instr(Instr), .Prev_byte(Prev_byte), .ImmSrc(ImmSrc), .ImmExt16(ImmExt16), .ImmExt(ImmExt));
  // Probe on PCTarget
  PCTargethandler pctargethandler_1 (
    .TEMPData(TEMP), .PCIn(PC), .PCTargetControl(PCTargetControl), .Imm(ImmExt16), .PCTarget(PCTarget),
    .TEMPOut(TEMPWD));
  // Probe on TEMPWD
  // Probe on ALUControl
  // Probe on CFControl
  LED led_2 (.in(IsSupported));
  // Probe on Branch
  // Probe on ResultSrc
  // Probe on MemWrite
  // Probe on ALUSrcA
  // Probe on ImmSrc
  // Probe on RegWrite
  // Probe on PC
  // Probe on RD
  // Probe on ACCData
  // Probe on ALUSrcB
  Adder #(.width(16)) adder_3 (.a(PC));  // open: b, out, cin, cout
  Multiplexer #(.enable("true"), .width(4)) multiplexer_2 (
    .in0(RD), .in1(ACCData), .out(SrcA), .sel(ALUSrcA));  // open: en
  Multiplexer #(.enable("true"), .width(8)) multiplexer_3 (
    .in0(ReadData), .in1(ImmExt), .out(SrcB), .sel(ALUSrcB));  // open: en
  // Probe on ALUControl
  // Probe on SrcA
  // Probe on SrcB
  // Probe on nothing
  // Probe on Zero
  alu alu_1 (
    .SrcA(SrcA), .SrcB(SrcB), .CF(CF), .ALUControl(ALUControl), .CFControl(CFControl), .Zero(Zero),
    .ALUResult(ALUResult), .CFOut(CF_ALUResult));
  // Probe on ALUResult
  Multiplexer #(.enable("true"), .width(8)) multiplexer_4 (
    .in0(RBRA), .in1(RDRC), .out(multiplexer_4_out), .sel(ConcatSrc));  // open: en
  or or_1 (PCSrc[1], Branch, Jump);
  // Probe on multiplexer_4_out
  // Probe on ALUResult
  // Probe on MemWrite
  datamem datamem_1 (.WD(ALUResult), .clk(clk), .A(multiplexer_4_out), .WE(MemWrite), .RD(ReadData));
  // Probe on ReadData
  // Probe on ResultSrc
  Multiplexer #(.enable("true"), .select(2), .width(16)) multiplexer_5 (
    .in0({ALUResult, {8{1'b0}}}), .in2(PCPlus8), .in3(PCPlus16), .out(Result), .sel(ResultSrc));  // open: in1, en
  // Probe on Result

  // Other names for the same wires on the sheet: CFIn = CF_ALUResult

  // Notes on the sheet:
  //   PC
  //   REGISTER FILE
  //   CONTROL
  //   ALU
  //   if branch/jump, switch PCSrc to PCTarget
  //   DATA MEMORY
endmodule

module regfile (
  input  [2:0] A1,
  input  [2:0] A3,
  input  [7:0] WD3,
  input  [15:0] TEMPIn,
  input  CFIn,
  input  [7:0] ACCIn,
  input  TEMPWrite,
  input  CFWrite,
  input  ACCWrite,
  input  WE3,
  input  Reset,
  input  CLK,
  output [3:0] RDOut,
  output [3:0] ACCOut,
  output [7:0] RBRAOut,
  output CFOut,
  output [7:0] RDRCOut,
  output [15:0] TEMPOut
);

  wire w0, w1, w2, w3, w4, w5, wr0, wr1, wr2, wr3, wr4, wr5;
  wire [3:0] o0, o1, o2, o3, o4, o5, o8;

  Decoder #(.select(3)) decoder_1 (
    .out0(wr0), .out1(wr1), .out2(wr2), .out3(wr3), .out4(wr4), .out5(wr5), .sel(A3));  // open: out6, out7, en
  Register #(.width(4)) RA (.D(WD3[3:0]), .en(w0), .clk(CLK), .Q(o0), .clr(Reset));
  Register #(.width(4)) RB (.D(WD3[3:0]), .en(w1), .clk(CLK), .Q(o1), .clr(Reset));
  Register #(.width(4)) RC (.D(WD3[3:0]), .en(w2), .clk(CLK), .Q(o2), .clr(Reset));
  Register #(.width(4)) RD (.D(WD3[3:0]), .en(w3), .clk(CLK), .Q(o3), .clr(Reset));
  Register #(.width(4)) RE (.D(WD3[3:0]), .en(w4), .clk(CLK), .Q(o4), .clr(Reset));
  Register #(.width(4)) ACC (.D(ACCIn[3:0]), .en(ACCWrite), .clk(CLK), .Q(ACCOut), .clr(Reset));
  Register #(.width(1)) CF (.D(CFIn), .en(CFWrite), .clk(CLK), .Q(CFOut), .clr(Reset));
  Register #(.width(16)) TEMP (.D(TEMPIn), .en(TEMPWrite), .clk(CLK), .Q(TEMPOut), .clr(Reset));
  and and_1 (w0, wr0, WE3);
  and and_2 (w1, wr1, WE3);
  and and_3 (w2, wr2, WE3);
  and and_4 (w3, wr3, WE3);
  and and_5 (w4, wr4, WE3);
  and and_6 (w5, wr5, WE3);
  Register #(.width(4)) IOA (.D(WD3[3:0]), .en(w5), .clk(CLK), .Q(o5), .clr(Reset));
  Multiplexer #(.enable("true"), .select(3), .width(4)) multiplexer_1 (
    .in0(o0), .in1(o1), .in2(o2), .in3(o3), .in4(o4), .in5(o5), .in6(o8), .out(RDOut), .sel(A1));  // open: in7, en
  ConcatInator concatinator_1 (.Arg1(o1), .Arg2(o0), .concat(RBRAOut));
  ConcatInator concatinator_2 (.Arg1(o3), .Arg2(o2), .concat(RDRCOut));

  // Other names for the same wires on the sheet: ACCIn_t[3:0] = ACCIn[3:0]; RD1[3:0] = RDOut; wACC = ACCWrite;
  //   wCF = CFWrite; wTEMP = TEMPWrite
endmodule

module aludecoder (
  input  [6:0] funct7,
  input  [2:0] funct3,
  input  [1:0] ALUOp,
  input  [3:0] opcode,
  output [2:0] ALUControl
);

  wire and_1_out, and_2_out, comparator_1_eq, comparator_2_eq, comparator_3_eq, comparator_4_eq,
       comparator_5_eq, comparator_6_eq, comparator_7_eq, comparator_8_eq, comparator_9_eq, comparator_10_eq,
       comparator_11_eq, comparator_12_eq, comparator_13_eq, comparator_14_eq, comparator_15_eq,
       comparator_16_eq, IsAdd, IsAnd, IsOr, IsSLT, IsSub, IsXor, not_1_out;
  wire [1:1] concat;

  Priority_Encoder priority_encoder_1 (
    .in0(IsAdd), .in1(IsSub), .in2(IsAnd), .in3(IsOr), .in5(IsSLT), .in7(IsXor), .out(ALUControl));  // open: in4, in6, en_in, gs, en_out
  Comparator #(.mode("unsigned"), .width(2)) comparator_1 (.a(ALUOp), .b(2'b00), .eq(comparator_1_eq));  // open: gt, lt
  Comparator #(.mode("unsigned"), .width(2)) comparator_2 (.a(ALUOp), .b(2'b10), .eq(comparator_2_eq));  // open: gt, lt
  Comparator #(.mode("unsigned"), .width(3)) comparator_3 (
    .a(funct3), .b(3'b000), .eq(comparator_3_eq));  // open: gt, lt
  not not_1 (not_1_out, comparator_4_eq);
  Comparator #(.mode("unsigned"), .width(2)) comparator_4 (
    .a({concat[1], funct7[5]}), .b(2'b11), .eq(comparator_4_eq));  // open: gt, lt
  Comparator #(.mode("unsigned"), .width(2)) comparator_5 (.a(ALUOp), .b(2'b01), .eq(comparator_5_eq));  // open: gt, lt
  Comparator #(.mode("unsigned"), .width(2)) comparator_6 (.a(ALUOp), .b(2'b10), .eq(comparator_6_eq));  // open: gt, lt
  Comparator #(.mode("unsigned"), .width(3)) comparator_7 (
    .a(funct3), .b(3'b000), .eq(comparator_7_eq));  // open: gt, lt
  Comparator #(.mode("unsigned"), .width(2)) comparator_8 (
    .a({concat[1], funct7[5]}), .b(2'b11), .eq(comparator_8_eq));  // open: gt, lt
  Comparator #(.mode("unsigned"), .width(2)) comparator_9 (.a(ALUOp), .b(2'b10), .eq(comparator_9_eq));  // open: gt, lt
  Comparator #(.mode("unsigned"), .width(3)) comparator_10 (
    .a(funct3), .b(3'b010), .eq(comparator_10_eq));  // open: gt, lt
  Comparator #(.mode("unsigned"), .width(2)) comparator_11 (
    .a(ALUOp), .b(2'b10), .eq(comparator_11_eq));  // open: gt, lt
  Comparator #(.mode("unsigned"), .width(3)) comparator_12 (
    .a(funct3), .b(3'b110), .eq(comparator_12_eq));  // open: gt, lt
  Comparator #(.mode("unsigned"), .width(2)) comparator_13 (
    .a(ALUOp), .b(2'b10), .eq(comparator_13_eq));  // open: gt, lt
  Comparator #(.mode("unsigned"), .width(3)) comparator_14 (
    .a(funct3), .b(3'b111), .eq(comparator_14_eq));  // open: gt, lt
  Comparator #(.mode("unsigned"), .width(2)) comparator_15 (
    .a(ALUOp), .b(2'b10), .eq(comparator_15_eq));  // open: gt, lt
  Comparator #(.mode("unsigned"), .width(3)) comparator_16 (
    .a(funct3), .b(3'b100), .eq(comparator_16_eq));  // open: gt, lt
  and and_1 (and_1_out, comparator_2_eq, comparator_3_eq, not_1_out);
  or or_1 (IsSub, comparator_5_eq, and_2_out);
  and and_2 (and_2_out, comparator_6_eq, comparator_7_eq, comparator_8_eq);
  and and_3 (IsSLT, comparator_9_eq, comparator_10_eq);
  and and_4 (IsOr, comparator_11_eq, comparator_12_eq);
  and and_5 (IsAnd, comparator_13_eq, comparator_14_eq);
  and and_6 (IsXor, comparator_15_eq, comparator_16_eq);
  or or_2 (IsAdd, comparator_1_eq, and_1_out);

  // Other names for the same wires on the sheet: concat[0] = funct7[5]; funct7_5 = funct7[5]; opcode_5 = concat[1]
endmodule

module alu (
  input  [3:0] SrcA,
  input  [7:0] SrcB,
  input  CF,
  input  [4:0] ALUControl,
  input  [3:0] CFControl,
  output Zero,
  output [7:0] ALUResult,
  output CFOut
);

  wire add_mxx_cf, addc_mxx_cf, bcd_CF, bcd_ISTRUE, comparator_1_gt, comparator_2_eq, comparator_3_eq,
       comparator_4_eq, multiplexer_1_out, not_1_out, or_3_out, sub_mxx_cf, subc_mxx_cf, subtractor_1_bout;
  wire [0:0] bbit, eqz4, eqzcf1, neqz4, neqzcf1;
  wire [3:0] sub_mxx_acc, subc_mxx_acc;
  wire [7:0] add_mxx_acc, addc_mxx_acc, adder_6_out, addimm, andd, bcd_ACC, dec_mxx_mem, dec_reg_RRR,
       inc_mxx_mem, inc_reg_RRR, orr, subimm, xorr;
  wire [8:0] adder_1_out, subtractor_1_out;
  wire [8:4] adder_5_out, subtractor_2_out;

  // Probe on {SrcA[2:0], SrcA[3]}
  // Probe on {SrcA[0], SrcA[3:1]}
  Adder #(.width(9)) adder_1 (.a({{5{1'b0}}, SrcA}), .b({1'b0, SrcB}), .out(adder_1_out));  // open: cin, cout
  Subtractor #(.width(9)) subtractor_1 (
    .a({{5{1'b0}}, SrcA}), .b({1'b0, SrcB}), .out(subtractor_1_out), .bout(subtractor_1_bout));  // open: bin
  Comparator #(.mode("unsigned"), .width(4)) comparator_1 (
    .a(SrcA), .b(4'b1010), .gt(comparator_1_gt));  // open: eq, lt
  Comparator #(.mode("unsigned"), .width(4)) comparator_2 (
    .a(SrcA), .b(4'b1010), .eq(comparator_2_eq));  // open: gt, lt
  Comparator #(.mode("unsigned"), .width(1)) comparator_3 (.a(CF), .b(1'b1), .eq(comparator_3_eq));  // open: gt, lt
  Adder adder_2 (.a(8'h1), .b(SrcB), .out(inc_mxx_mem));  // open: cin, cout
  Adder adder_3 (.a(8'h1), .b({4'b0000, SrcA}), .out(inc_reg_RRR));  // open: cin, cout
  assign andd = {4'b0000, SrcA} & SrcB;  // AND_Gate and_1, 8 bits wide
  assign orr = {4'b0000, SrcA} | SrcB;  // OR_Gate or_1, 8 bits wide
  or or_2 (bcd_ISTRUE, comparator_1_gt, comparator_2_eq, comparator_3_eq);
  Adder #(.width(9)) adder_4 (
    .a(adder_1_out), .b({{8{1'b0}}, CF}), .out({addc_mxx_acc[7:4], addc_mxx_cf, addc_mxx_acc[3:0]}));  // open: cin, cout
  Adder #(.width(9)) adder_5 (
    .a(subtractor_1_out), .b({{8{1'b0}}, CF}), .out({adder_5_out, subc_mxx_acc}));  // open: cin, cout
  Multiplexer #(.enable("true"), .select(2)) multiplexer_1 (
    .in0(SrcA[0]), .in1(SrcA[1]), .in2(SrcA[2]), .in3(SrcA[3]), .out(multiplexer_1_out), .sel(SrcB[1:0]));  // open: en
  Comparator #(.mode("unsigned"), .width(9)) comparator_4 (
    .a({adder_5_out, subc_mxx_acc}), .b({9{1'b0}}), .eq(comparator_4_eq));  // open: gt, lt
  Comparator #(.mode("unsigned"), .width(1)) comparator_5 (
    .a(multiplexer_1_out), .b(1'b1), .eq(bbit[0]));  // open: gt, lt
  not not_1 (not_1_out, comparator_4_eq);
  and and_2 (subc_mxx_cf, not_1_out, subtractor_1_bout);
  Adder adder_6 (.a({4'b0000, SrcA}), .b(8'h6), .out(adder_6_out));  // open: cin, cout
  Multiplexer #(.enable("true")) multiplexer_2 (.in0(1'b0), .in1(1'b1), .out(bcd_CF), .sel(bcd_ISTRUE));  // open: en
  // Probe on ALUResult
  Multiplexer #(.enable("true"), .select(5), .width(8)) multiplexer_3 (
    .in0({4'b0000, SrcA[0], SrcA[3:1]}), .in1({4'b0000, SrcA[2:0], SrcA[3]}), .in2({4'b0000, CF, SrcA[3:1]}),
    .in3({4'b0000, SrcA[2:0], CF}), .in4(SrcB), .in5({4'b0000, SrcA}), .in6(addc_mxx_acc), .in7(add_mxx_acc),
    .in8({4'b0000, subc_mxx_acc}), .in9({4'b0000, sub_mxx_acc}), .in10(inc_mxx_mem), .in11(dec_mxx_mem),
    .in12(inc_reg_RRR), .in13(dec_reg_RRR), .in14(andd), .in15(xorr), .in16(orr), .in17(bcd_ACC),
    .in18(addimm), .in19(subimm), .in20({{7{1'b0}}, bbit[0]}), .in21({{7{1'b0}}, neqz4[0]}),
    .in22({{7{1'b0}}, eqz4[0]}), .in23({{7{1'b0}}, eqzcf1[0]}), .in24({{7{1'b0}}, neqzcf1[0]}),
    .out(ALUResult), .sel(ALUControl));  // open: in25, in26, in27, in28, in29, in30, in31, en
  // Probe on ALUControl
  Multiplexer #(.enable("true"), .width(8)) multiplexer_4 (
    .in0({4'b0000, SrcA}), .in1(adder_6_out), .out(bcd_ACC), .sel(bcd_ISTRUE));  // open: en
  assign xorr = {4'b0000, SrcA} ^ SrcB;  // XOR_Gate xor_1, 8 bits wide
  Adder #(.width(9)) adder_7 (
    .a({{5{1'b0}}, SrcA}), .b({1'b0, SrcB}), .out({add_mxx_acc[7:4], add_mxx_cf, add_mxx_acc[3:0]}));  // open: cin, cout
  Subtractor #(.width(9)) subtractor_2 (
    .a({{5{1'b0}}, SrcA}), .b({1'b0, SrcB}), .out({subtractor_2_out, sub_mxx_acc}), .bout(sub_mxx_cf));  // open: bin
  Subtractor subtractor_3 (.a(SrcB), .b(8'h1), .out(dec_mxx_mem));  // open: bin, bout
  Subtractor subtractor_4 (.a({4'b0000, SrcA}), .b(8'h1), .out(dec_reg_RRR));  // open: bin, bout
  not not_2 (neqz4[0], eqz4[0]);
  Comparator #(.mode("unsigned"), .width(4)) comparator_6 (.a(SrcA), .b(4'b0000), .eq(eqz4[0]));  // open: gt, lt
  Comparator #(.mode("unsigned"), .width(1)) comparator_7 (.a(CF), .b(1'b0), .eq(eqzcf1[0]));  // open: gt, lt
  or or_3 (or_3_out, ALUResult[0], ALUResult[1], ALUResult[2], ALUResult[3], ALUResult[5], ALUResult[6], ALUResult[7], ALUResult[4]);
  not not_3 (neqzcf1[0], eqzcf1[0]);
  Multiplexer #(.enable("true"), .select(4)) multiplexer_5 (
    .in0(SrcA[3]), .in1(SrcA[0]), .in2(addc_mxx_cf), .in3(add_mxx_cf), .in4(subc_mxx_cf), .in5(sub_mxx_cf),
    .in6(1'b0), .in7(1'b1), .in8(bcd_CF), .out(CFOut), .sel(CFControl));  // open: in9, in10, in11, in12, in13, in14, in15, en
  // Probe on CFControl
  not not_4 (Zero, or_3_out);
  Adder adder_8 (.a(SrcB), .b({4'b0000, SrcA}), .out(addimm));  // open: cin, cout
  Subtractor subtractor_5 (.a({4'b0000, SrcA}), .b(SrcB), .out(subimm));  // open: bin, bout

  // Other names for the same wires on the sheet: LW[7:0] = SrcB; fourrrotleft[3:0] = {SrcA[2:0], SrcA[3]};
  //   fourrrotright[3:0] = {SrcA[0], SrcA[3:1]}; from_reg[3:0] = SrcA; rotleft5_ACC[3:0] = {SrcA[2:0], CF};
  //   rotright5_CF = SrcA[0]; SW[3:0] = SrcA; to_reg[3:0] = SrcA; rotright5_ACC[3:0] = {CF, SrcA[3:1]};
  //   rotleft5_CF = SrcA[3]

  // Notes on the sheet:
  //   acc
  //   mem
  //   acc
  //   mem
  //   fourrotleft
  //   fourrotright
  //   Load from mem/imm to reg
  //   RRR
  //   Input
  //   AND
  //   orr
  //   to-reg
  //   cf = 0
  //   addc-mxx
  //   subc-mxx
  //   inc_mxx
  //   inc_reg
  //   bcd
  //   bbit
  //   ALUResult (excluding CF)
  //   fiverotleft
  //   fiverotright
  //   Store from reg to reg/mem
  //   acc
  //   mem
  //   from-reg
  //   cf = 1
  //   RRR
  //   XOR
  //   Output
  //   acc
  //   mem
  //   add-mxx
  //   sub-mxx
  //   dec_mxx
  //   dec_reg
  //   4bit == 0
  //   CFOut (or CFResult)
  //   Zero
  //   addimm
  //   subimm
endmodule

module instmem (
  input  [15:0] Address,
  output [7:0] Instr
);

  ROM #(.addrWidth(16)) rom_1 (.addr(Address), .data(Instr));

  // Notes on the sheet:
  //   // Nasty hack to make word-addressable ROM usable
  //   contents of rom_1 (hex, n*v repeats v):
  //   ff ff ff
endmodule

module datamem (
  input  WE,
  input  [7:0] A,
  input  [7:0] WD,
  input  clk,
  output [7:0] RD
);

  RAM #(.asyncread("true")) ram_1 (.addr(A), .we(WE), .oe(1'b1), .clk(clk), .din(WD), .dout(RD));

  // Other names for the same wires on the sheet: WriteData[7:0] = WD; WriteEnable = WE

  // Notes on the sheet:
  //   // Nasty hack to make word-addressable RAM usable
endmodule

module extender (
  input  [7:0] Instr,
  input  [7:0] Prev_byte,
  input  [2:0] ImmSrc,
  output [15:0] ImmExt16,
  output [7:0] ImmExt
);

  wire [15:0] undriven, undriven_2;

  // Probe on {4'b0000, Prev_byte[3:0], Instr}
  Multiplexer #(.enable("true"), .select(3), .width(8)) multiplexer_1 (
    .in0({4'b0000, Instr[3:0]}), .in1({{6{1'b0}}, Instr[4:3]}), .out(ImmExt), .sel(ImmSrc));  // open: in2, in3, in4, in5, in6, in7, en
  Multiplexer #(.enable("true"), .select(3), .width(16)) multiplexer_2 (
    .in0(undriven), .in1(undriven_2), .in2({{5{1'b0}}, Prev_byte[2:0], Instr}),
    .in3({4'b0000, Prev_byte[3:0], Instr}), .out(ImmExt16), .sel(ImmSrc));  // open: in4, in5, in6, in7, en

  // Other names for the same wires on the sheet: elevenbits[10:0] = {Prev_byte[2:0], Instr};
  //   fourbits[3:0] = Instr[3:0]; twelvebits[11:0] = {Prev_byte[3:0], Instr}; twobits[1:0] = Instr[4:3]

  // Notes on the sheet:
  //   2 bit
  //   11 bit
  //   Input
  //   4 bit
  //   12 bit
  //   Output
endmodule

module maindecoder (
  input  [7:0] Inst,
  input  Is2ndbyte,
  input  [7:0] Prev_byte,
  input  Branch_result,
  output IsSupported,
  output Branch,
  output [1:0] ResultSrc,
  output MemWrite,
  output ALUSrcA,
  output [2:0] ImmSrc,
  output RegWrite,
  output Jump,
  output CFWrite,
  output TEMPWrite,
  output Is1byte,
  output Is2byte,
  output [3:0] CFControl,
  output [4:0] ALUControl,
  output ALUSrcB,
  output ACCWrite,
  output ConcatSrc,
  output [2:0] rs,
  output [2:0] rd,
  output [1:0] PCTargetControl,
  output Power
);

  wire and_3_out, and_4_out, and_5_out, and_6_out, and_15_out, and_16_out, and_17_out, and_18_out,
       and_19_out, and_20_out, and_21_out, and_22_out, comparator_1_eq, comparator_2_eq, comparator_3_eq,
       comparator_4_lt, comparator_5_eq, comparator_6_eq, comparator_7_eq, comparator_8_eq, comparator_9_eq,
       comparator_10_eq, comparator_11_eq, comparator_12_eq, comparator_13_eq, comparator_14_eq,
       comparator_15_eq, comparator_16_eq, comparator_17_eq, comparator_18_eq, comparator_19_eq,
       comparator_20_eq, comparator_21_eq, comparator_22_eq, comparator_23_lt, comparator_24_eq,
       comparator_25_eq, comparator_26_lt, comparator_27_eq, comparator_28_eq, comparator_29_eq,
       comparator_30_eq, comparator_31_eq, comparator_32_eq, comparator_33_eq, comparator_34_eq,
       comparator_35_lt, comparator_36_eq, comparator_37_eq, comparator_38_lt, comparator_39_eq,
       comparator_40_eq, comparator_41_eq, comparator_42_eq, comparator_43_eq, comparator_44_eq,
       comparator_45_eq, comparator_46_eq, comparator_47_eq, comparator_48_eq, comparator_49_eq,
       comparator_50_eq, comparator_51_eq, comparator_52_eq, comparator_53_eq, comparator_54_eq,
       comparator_55_eq, comparator_56_eq, comparator_57_eq, comparator_58_eq, comparator_59_eq,
       comparator_60_eq, comparator_61_eq, comparator_62_eq, comparator_63_eq, comparator_64_eq,
       comparator_65_eq, comparator_66_eq, comparator_67_eq, comparator_68_eq, comparator_69_eq,
       comparator_70_eq, comparator_71_eq, comparator_72_eq, comparator_73_eq, comparator_74_eq,
       comparator_75_eq, comparator_76_eq, comparator_77_eq, comparator_78_eq, comparator_79_eq,
       comparator_80_eq, comparator_81_eq, comparator_82_eq, comparator_83_eq, comparator_84_eq,
       comparator_85_eq, decreg_out, fourbiteqz_out, fourbitnz_out, increg_out, Is2bitimm, Is4bitimm,
       Is11bitimm, Is12bitimm, Isacc_imm, Isadd_imm, Isadd_mba, Isaddc_mba, Isand_ba, Isand_imm, Isand_mba,
       Isb_a, Isb_b, Isbbit_kimm_a, Isbbit_kimm_b, Isbcd, Isbeqz_a, Isbeqz_b, Isbeqzcf_a, Isbeqzcf_b,
       Isbnez_a, Isbnez_b, Isbnezcf_a, Isbnezcf_b, Isbnza_a, Isbnza_b, Isbnzb_a, Isbnzb_b, Isbnzd_a,
       Isbnzd_b, Iscall_a, Iscall_b, Isclr_cf, Isdec, Isdec_mba, Isdec_mdc, Isdec_reg, Isfrom_ioa,
       Isfrom_mba, Isfrom_mdc, Isfrom_reg, Isinc, Isinc_mba, Isinc_mdc, Isinc_reg, IsLW, Isnop, Isor_ba,
       Isor_imm, Isor_mba, IsPCTarget1, IsPCTarget2, Isr4_imm, Israrb_imm_a, Israrb_imm_b, Isrcrd_imm_a,
       Isrcrd_imm_b, Isret, Isrotl, Isrotlc, Isrotr, Isrotrc, IsRRR, Isset_cf, IsShutdown_A, IsShutdown_B,
       Issub_imm, Issub_mba, Issubc_mba, Isto_mba, Isto_mdc, Isto_reg, Isxor_ba, Isxor_imm, Isxor_mba,
       not_1_out, not_2_out, not_3_out, not_4_out, not_5_out, not_6_out, not_7_out, not_8_out, not_9_out,
       not_10_out, not_11_out, not_12_out, not_13_out, not_14_out, not_15_out, not_16_out, not_17_out,
       not_18_out, not_19_out, not_20_out, not_21_out, not_22_out, not_23_out, not_24_out, not_25_out,
       not_26_out, not_27_out, not_28_out, not_29_out, not_30_out, not_31_out, not_32_out, not_33_out,
       not_34_out, not_35_out, not_36_out, not_37_out, not_38_out, not_39_out, not_40_out, not_41_out,
       or_1_out, or_3_out, or_4_out, or_5_out, or_6_out, or_7_out, store_out;
  wire [2:0] priority_encoder_4_out, priority_encoder_5_out;

  Comparator #(.mode("unsigned")) comparator_1 (.a(Inst), .b(8'h37), .eq(comparator_1_eq));  // open: gt, lt
  Comparator #(.mode("unsigned")) comparator_2 (.a(Inst), .b(8'h3e), .eq(comparator_2_eq));  // open: gt, lt
  Comparator #(.mode("unsigned")) comparator_3 (.a(Prev_byte), .b(8'h37), .eq(comparator_3_eq));  // open: gt, lt
  and and_1 (IsShutdown_A, comparator_1_eq, not_1_out);
  not not_1 (not_1_out, Is2ndbyte);
  and and_2 (IsShutdown_B, comparator_2_eq, comparator_3_eq, Is2ndbyte);
  Comparator #(.mode("unsigned"), .width(4)) comparator_4 (
    .a(Inst[7:4]), .b(4'b0011), .lt(comparator_4_lt));  // open: gt, eq
  Comparator #(.mode("unsigned"), .width(4)) comparator_5 (
    .a(Inst[7:4]), .b(4'b0111), .eq(comparator_5_eq));  // open: gt, lt
  Comparator #(.mode("unsigned"), .width(4)) comparator_6 (
    .a(Inst[7:4]), .b(4'b0011), .eq(comparator_6_eq));  // open: gt, lt
  not not_2 (not_2_out, IsShutdown_A);
  not not_3 (not_3_out, IsShutdown_B);
  not not_4 (not_4_out, Is2ndbyte);
  // Probe on Inst[3:1]
  and and_3 (and_3_out, comparator_4_lt, not_5_out);
  not not_5 (not_5_out, Is2ndbyte);
  and and_4 (and_4_out, comparator_5_eq, not_6_out);
  not not_6 (not_6_out, Is2ndbyte);
  and and_5 (and_5_out, comparator_6_eq, not_2_out, not_3_out);
  or or_1 (or_1_out, and_3_out, and_4_out);
  or or_2 (Is1byte, or_1_out, and_6_out);
  and and_6 (and_6_out, and_5_out, not_4_out);
  Comparator #(.mode("unsigned")) comparator_7 (.a(Inst), .b({8{1'b0}}), .eq(comparator_7_eq));  // open: gt, lt
  not not_7 (not_7_out, Is2ndbyte);
  Comparator #(.mode("unsigned")) comparator_8 (.a(Inst), .b(8'h1), .eq(comparator_8_eq));  // open: gt, lt
  not not_8 (not_8_out, Is2ndbyte);
  Comparator #(.mode("unsigned")) comparator_9 (.a(Inst), .b(8'h2), .eq(comparator_9_eq));  // open: gt, lt
  not not_9 (not_9_out, Is2ndbyte);
  Comparator #(.mode("unsigned")) comparator_10 (.a(Inst), .b(8'h3), .eq(comparator_10_eq));  // open: gt, lt
  not not_10 (not_10_out, Is2ndbyte);
  Comparator #(.mode("unsigned")) comparator_11 (.a(Inst), .b(8'h4), .eq(comparator_11_eq));  // open: gt, lt
  not not_11 (not_11_out, Is2ndbyte);
  Comparator #(.mode("unsigned")) comparator_12 (.a(Inst), .b(8'h5), .eq(comparator_12_eq));  // open: gt, lt
  not not_12 (not_12_out, Is2ndbyte);
  Comparator #(.mode("unsigned")) comparator_13 (.a(Inst), .b(8'h6), .eq(comparator_13_eq));  // open: gt, lt
  not not_13 (not_13_out, Is2ndbyte);
  Comparator #(.mode("unsigned")) comparator_14 (.a(Inst), .b(8'h7), .eq(comparator_14_eq));  // open: gt, lt
  not not_14 (not_14_out, Is2ndbyte);
  or increg (increg_out, Isinc_reg, Isinc);
  or decreg (decreg_out, Isdec_reg, Isdec);
  and and_7 (Isrotr, comparator_7_eq, not_7_out);
  and and_8 (Isrotl, comparator_8_eq, not_8_out);
  and and_9 (Isrotrc, comparator_9_eq, not_9_out);
  and and_10 (Isrotlc, comparator_10_eq, not_10_out);
  and and_11 (Isfrom_mba, comparator_11_eq, not_11_out);
  and and_12 (Isto_mba, comparator_12_eq, not_12_out);
  and and_13 (Isfrom_mdc, comparator_13_eq, not_13_out);
  and and_14 (Isto_mdc, comparator_14_eq, not_14_out);
  or store (store_out, Isto_mba, Isto_reg, Isfrom_ioa, Isfrom_reg, Isto_mdc);
  or or_3 (or_3_out, Isinc_mba, Isinc_mdc);
  or or_4 (or_4_out, Isdec_mba, Isdec_mdc);
  and and_15 (and_15_out, Branch_result, Isbbit_kimm_b);
  and and_16 (and_16_out, Branch_result, Isbnza_b);
  and and_17 (and_17_out, Branch_result, Isbnzb_b);
  and and_18 (and_18_out, Branch_result, Isbeqz_b);
  and and_19 (and_19_out, Branch_result, Isbnez_b);
  and and_20 (and_20_out, Branch_result, Isbeqzcf_b);
  and and_21 (and_21_out, Branch_result, Isbnezcf_b);
  and and_22 (and_22_out, Branch_result, Isbnzd_b);
  Comparator #(.mode("unsigned")) comparator_15 (.a(Inst), .b(8'h8), .eq(comparator_15_eq));  // open: gt, lt
  Comparator #(.mode("unsigned")) comparator_16 (.a(Inst), .b(8'h9), .eq(comparator_16_eq));  // open: gt, lt
  Comparator #(.mode("unsigned")) comparator_17 (.a(Inst), .b(8'ha), .eq(comparator_17_eq));  // open: gt, lt
  Comparator #(.mode("unsigned")) comparator_18 (.a(Inst), .b(8'hb), .eq(comparator_18_eq));  // open: gt, lt
  Comparator #(.mode("unsigned")) comparator_19 (.a(Inst), .b(8'hc), .eq(comparator_19_eq));  // open: gt, lt
  Comparator #(.mode("unsigned")) comparator_20 (.a(Inst), .b(8'hd), .eq(comparator_20_eq));  // open: gt, lt
  Comparator #(.mode("unsigned")) comparator_21 (.a(Inst), .b(8'he), .eq(comparator_21_eq));  // open: gt, lt
  Comparator #(.mode("unsigned")) comparator_22 (.a(Inst), .b(8'hf), .eq(comparator_22_eq));  // open: gt, lt
  or or_5 (or_5_out, Isand_ba, Isand_mba, Isand_imm);
  or or_6 (or_6_out, Isxor_ba, Isxor_mba, Isxor_imm);
  or or_7 (or_7_out, Isor_ba, Isor_mba, Isor_imm);
  or fourbitnz (fourbitnz_out, Isbnza_a, Isbnzb_a, Isbnez_a, Isbnzd_a, Isbnzd_b);
  buf fourbiteqz (fourbiteqz_out, Isbeqz_a);  // OR_Gate
  and and_23 (Isaddc_mba, comparator_15_eq, not_15_out);
  not not_15 (not_15_out, Is2ndbyte);
  and and_24 (Isadd_mba, comparator_16_eq, not_16_out);
  not not_16 (not_16_out, Is2ndbyte);
  and and_25 (Issubc_mba, comparator_17_eq, not_17_out);
  not not_17 (not_17_out, Is2ndbyte);
  and and_26 (Issub_mba, comparator_18_eq, not_18_out);
  not not_18 (not_18_out, Is2ndbyte);
  and and_27 (Isinc_mba, comparator_19_eq, not_19_out);
  not not_19 (not_19_out, Is2ndbyte);
  and and_28 (Isdec_mba, comparator_20_eq, not_20_out);
  not not_20 (not_20_out, Is2ndbyte);
  and and_29 (Isinc_mdc, comparator_21_eq, not_21_out);
  not not_21 (not_21_out, Is2ndbyte);
  and and_30 (Isdec_mdc, comparator_22_eq, not_22_out);
  not not_22 (not_22_out, Is2ndbyte);
  or load (IsLW, Isfrom_mba, Isr4_imm, Israrb_imm_a, Isfrom_mdc, Israrb_imm_b, Isrcrd_imm_a, Isrcrd_imm_b, Isacc_imm);
  or or_8 (RegWrite, Isinc_reg, Isdec_reg, Isto_reg, Isr4_imm, Israrb_imm_a, Israrb_imm_b, Isrcrd_imm_a, Isrcrd_imm_b);
  or or_9 (TEMPWrite, Isret, Iscall_b, 1'b0);
  or or_10 (Branch, and_15_out, and_16_out, and_17_out, and_18_out, and_19_out, and_20_out, and_21_out, and_22_out, Isb_b, Iscall_b);
  Priority_Encoder #(.select(5)) priority_encoder_1 (
    .in0(Isrotr), .in1(Isrotl), .in2(Isrotrc), .in3(Isrotlc), .in4(IsLW), .in5(store_out), .in6(Isaddc_mba),
    .in7(Isadd_mba), .in8(Issubc_mba), .in9(Issub_mba), .in10(or_3_out), .in11(or_4_out), .in12(increg_out),
    .in13(decreg_out), .in14(or_5_out), .in15(or_6_out), .in16(or_7_out), .in17(Isbcd), .in18(Isadd_imm),
    .in19(Issub_imm), .in20(Isbbit_kimm_a), .in21(fourbitnz_out), .in22(fourbiteqz_out), .in23(Isbeqzcf_a),
    .in24(Isbnezcf_a), .out(ALUControl));  // open: in25, in26, in27, in28, in29, in30, in31, gs, en_out, en_in
  // Probe on ALUControl
  Comparator #(.mode("unsigned"), .width(3)) comparator_23 (
    .a(Inst[3:1]), .b(3'b101), .lt(comparator_23_lt));  // open: gt, eq
  Comparator #(.mode("unsigned"), .width(4)) comparator_24 (
    .a(Inst[7:4]), .b(4'b0001), .eq(comparator_24_eq));  // open: gt, lt
  Comparator #(.mode("unsigned"), .width(1)) comparator_25 (
    .a(Inst[0]), .b(1'b0), .eq(comparator_25_eq));  // open: gt, lt
  not not_23 (not_23_out, Is2ndbyte);
  Comparator #(.mode("unsigned"), .width(3)) comparator_26 (
    .a(Inst[3:1]), .b(3'b101), .lt(comparator_26_lt));  // open: gt, eq
  Comparator #(.mode("unsigned"), .width(4)) comparator_27 (
    .a(Inst[7:4]), .b(4'b0001), .eq(comparator_27_eq));  // open: gt, lt
  Comparator #(.mode("unsigned"), .width(1)) comparator_28 (
    .a(Inst[0]), .b(1'b1), .eq(comparator_28_eq));  // open: gt, lt
  not not_24 (not_24_out, Is2ndbyte);
  Comparator #(.mode("unsigned")) comparator_29 (.a(Inst), .b(8'h1a), .eq(comparator_29_eq));  // open: gt, lt
  not not_25 (not_25_out, Is2ndbyte);
  Comparator #(.mode("unsigned")) comparator_30 (.a(Inst), .b(8'h1b), .eq(comparator_30_eq));  // open: gt, lt
  not not_26 (not_26_out, Is2ndbyte);
  Comparator #(.mode("unsigned")) comparator_31 (.a(Inst), .b(8'h1c), .eq(comparator_31_eq));  // open: gt, lt
  not not_27 (not_27_out, Is2ndbyte);
  Comparator #(.mode("unsigned")) comparator_32 (.a(Inst), .b(8'h1d), .eq(comparator_32_eq));  // open: gt, lt
  not not_28 (not_28_out, Is2ndbyte);
  Comparator #(.mode("unsigned")) comparator_33 (.a(Inst), .b(8'h1e), .eq(comparator_33_eq));  // open: gt, lt
  not not_29 (not_29_out, Is2ndbyte);
  Comparator #(.mode("unsigned")) comparator_34 (.a(Inst), .b(8'h1f), .eq(comparator_34_eq));  // open: gt, lt
  not not_30 (not_30_out, Is2ndbyte);
  Priority_Encoder #(.select(4)) priority_encoder_2 (
    .in0(Isrotrc), .in1(Isrotlc), .in2(Isaddc_mba), .in3(Isadd_mba), .in4(Issubc_mba), .in5(Issub_mba),
    .in6(Isclr_cf), .in7(Isset_cf), .in8(Isbcd), .out(CFControl));  // open: in9, in10, in11, in12, in13, in14, in15, gs, en_out, en_in
  and and_31 (Isinc_reg, comparator_23_lt, comparator_24_eq, comparator_25_eq, not_23_out);
  and and_32 (Isdec_reg, comparator_26_lt, comparator_27_eq, comparator_28_eq, not_24_out);
  and and_33 (Isand_ba, comparator_29_eq, not_25_out);
  and and_34 (Isxor_ba, comparator_30_eq, not_26_out);
  and and_35 (Isor_ba, comparator_31_eq, not_27_out);
  and and_36 (Isand_mba, comparator_32_eq, not_28_out);
  and and_37 (Isxor_mba, comparator_33_eq, not_29_out);
  and and_38 (Isor_mba, comparator_34_eq, not_30_out);
  // Probe on CFControl
  or or_11 (IsPCTarget1, Isbbit_kimm_b, Isbnza_b, Isbnzb_b, Isbnzd_b, Isbeqz_b, Isbnez_b, Isbeqzcf_b, Isbnezcf_b);
  or or_12 (MemWrite, Isto_mba, Isto_mdc, Isinc_mba, Isdec_mba, Isinc_mdc, Isdec_mdc, Isand_mba, Isxor_mba, Isor_mba, 1'b0);
  or or_13 (CFWrite, Isrotrc, Isrotlc, Isaddc_mba, Isadd_mba, Issubc_mba, Issub_mba, Isclr_cf, Isset_cf, Isbcd, 1'b0);
  or or_14 (Jump, Isret, 1'b0);
  Comparator #(.mode("unsigned"), .width(3)) comparator_35 (
    .a(Inst[3:1]), .b(3'b101), .lt(comparator_35_lt));  // open: gt, eq
  Comparator #(.mode("unsigned"), .width(4)) comparator_36 (
    .a(Inst[7:4]), .b(4'b0010), .eq(comparator_36_eq));  // open: gt, lt
  Comparator #(.mode("unsigned"), .width(1)) comparator_37 (
    .a(Inst[0]), .b(1'b0), .eq(comparator_37_eq));  // open: gt, lt
  not not_31 (not_31_out, Is2ndbyte);
  Comparator #(.mode("unsigned"), .width(3)) comparator_38 (
    .a(Inst[3:1]), .b(3'b101), .lt(comparator_38_lt));  // open: gt, eq
  Comparator #(.mode("unsigned"), .width(4)) comparator_39 (
    .a(Inst[7:4]), .b(4'b0010), .eq(comparator_39_eq));  // open: gt, lt
  Comparator #(.mode("unsigned"), .width(1)) comparator_40 (
    .a(Inst[0]), .b(1'b1), .eq(comparator_40_eq));  // open: gt, lt
  not not_32 (not_32_out, Is2ndbyte);
  Comparator #(.mode("unsigned")) comparator_41 (.a(Inst), .b(8'h2a), .eq(comparator_41_eq));  // open: gt, lt
  not not_33 (not_33_out, Is2ndbyte);
  Comparator #(.mode("unsigned")) comparator_42 (.a(Inst), .b(8'h2b), .eq(comparator_42_eq));  // open: gt, lt
  not not_34 (not_34_out, Is2ndbyte);
  Comparator #(.mode("unsigned")) comparator_43 (.a(Inst), .b(8'h2e), .eq(comparator_43_eq));  // open: gt, lt
  not not_35 (not_35_out, Is2ndbyte);
  Comparator #(.mode("unsigned")) comparator_44 (.a(Inst), .b(8'h32), .eq(comparator_44_eq));  // open: gt, lt
  not not_36 (not_36_out, Is2ndbyte);
  Comparator #(.mode("unsigned")) comparator_45 (.a(Inst), .b(8'h31), .eq(comparator_45_eq));  // open: gt, lt
  not not_37 (not_37_out, Is2ndbyte);
  and and_39 (Isto_reg, comparator_35_lt, comparator_36_eq, comparator_37_eq, not_31_out);
  and and_40 (Isfrom_reg, comparator_38_lt, comparator_39_eq, comparator_40_eq, not_32_out);
  and and_41 (Isclr_cf, comparator_41_eq, not_33_out);
  and and_42 (Isset_cf, comparator_42_eq, not_34_out);
  and and_43 (Isret, comparator_43_eq, not_35_out);
  and and_44 (Isfrom_ioa, comparator_44_eq, not_36_out);
  and and_45 (Isinc, comparator_45_eq, not_37_out);
  or or_15 (IsPCTarget2, Isb_b, Iscall_b);
  or or_16 (ALUSrcB, Isbbit_kimm_a, Isadd_imm, Issub_imm, Isand_imm, Isxor_imm, Isor_imm, Isr4_imm, Israrb_imm_a, Israrb_imm_b, Isrcrd_imm_a, Isrcrd_imm_b, Isacc_imm);
  or or_17 (ALUSrcA, Isrotr, Isrotl, Isrotrc, Isrotlc, Isto_mba, Isto_mdc, Isaddc_mba, Isadd_mba, Issubc_mba, Issub_mba, Isand_ba, Isxor_ba, Isor_ba, Isand_mba, Isxor_mba, Isor_mba, Isinc, Isbcd, Isdec, Isadd_imm, Issub_imm, Isand_imm, Isxor_imm, Isor_imm, Isbbit_kimm_a, Isbeqz_a, Isbnez_a, 1'b0);
  Comparator #(.mode("unsigned")) comparator_46 (.a(Inst), .b(8'h36), .eq(comparator_46_eq));  // open: gt, lt
  not not_38 (not_38_out, Is2ndbyte);
  Comparator #(.mode("unsigned")) comparator_47 (.a(Inst), .b(8'h3e), .eq(comparator_47_eq));  // open: gt, lt
  not not_39 (not_39_out, Is2ndbyte);
  Comparator #(.mode("unsigned")) comparator_48 (.a(Inst), .b(8'h3f), .eq(comparator_48_eq));  // open: gt, lt
  not not_40 (not_40_out, Is2ndbyte);
  Comparator #(.mode("unsigned"), .width(4)) comparator_49 (
    .a(Inst[7:4]), .b(4'b0111), .eq(comparator_49_eq));  // open: gt, lt
  not not_41 (not_41_out, Is2ndbyte);
  or or_18 (ACCWrite, Isrotr, Isrotl, Isrotrc, Isrotlc, Isfrom_mba, Isfrom_mdc, Isaddc_mba, Isadd_mba, Issubc_mba, Issub_mba, Isand_ba, Isxor_ba, Isor_ba, Isfrom_reg, Isfrom_ioa, Isinc, Isbcd, Isdec, Isadd_imm, Issub_imm, Isand_imm, Isxor_imm, Isor_imm, Isacc_imm);
  and and_46 (Isbcd, comparator_46_eq, not_38_out);
  and and_47 (Isnop, comparator_47_eq, not_39_out);
  and and_48 (Isdec, comparator_48_eq, not_40_out);
  and and_49 (Isacc_imm, comparator_49_eq, not_41_out);
  Priority_Encoder #(.select(2)) priority_encoder_3 (
    .in0(Isret), .in1(IsPCTarget1), .in2(IsPCTarget2), .out(PCTargetControl));  // open: in3, gs, en_out, en_in
  or or_19 (IsRRR, Isinc_reg, Isdec_reg, Isto_reg, Isfrom_reg);
  or or_20 (ConcatSrc, Isfrom_mdc, Isto_mdc, Isinc_mdc, Isdec_mdc, 1'b0);
  or or_21 (Is4bitimm, Isadd_imm, Issub_imm, Isand_imm, Isxor_imm, Isor_imm, Isr4_imm, Israrb_imm_a, Israrb_imm_b, Isrcrd_imm_a, Isrcrd_imm_b, Isacc_imm);
  buf or_22 (Is2bitimm, Isbbit_kimm_a);  // OR_Gate
  Comparator #(.mode("unsigned")) comparator_50 (.a(Prev_byte), .b(8'h40), .eq(comparator_50_eq));  // open: gt, lt
  Comparator #(.mode("unsigned"), .width(4)) comparator_51 (
    .a(Inst[7:4]), .b(4'b0000), .eq(comparator_51_eq));  // open: gt, lt
  Comparator #(.mode("unsigned")) comparator_52 (.a(Prev_byte), .b(8'h41), .eq(comparator_52_eq));  // open: gt, lt
  Comparator #(.mode("unsigned"), .width(4)) comparator_53 (
    .a(Inst[7:4]), .b(4'b0000), .eq(comparator_53_eq));  // open: gt, lt
  Comparator #(.mode("unsigned")) comparator_54 (.a(Prev_byte), .b(8'h42), .eq(comparator_54_eq));  // open: gt, lt
  Comparator #(.mode("unsigned"), .width(4)) comparator_55 (
    .a(Inst[7:4]), .b(4'b0000), .eq(comparator_55_eq));  // open: gt, lt
  Comparator #(.mode("unsigned")) comparator_56 (.a(Prev_byte), .b(8'h43), .eq(comparator_56_eq));  // open: gt, lt
  Comparator #(.mode("unsigned"), .width(4)) comparator_57 (
    .a(Inst[7:4]), .b(4'b0000), .eq(comparator_57_eq));  // open: gt, lt
  Comparator #(.mode("unsigned")) comparator_58 (.a(Prev_byte), .b(8'h44), .eq(comparator_58_eq));  // open: gt, lt
  Comparator #(.mode("unsigned"), .width(4)) comparator_59 (
    .a(Inst[7:4]), .b(4'b0000), .eq(comparator_59_eq));  // open: gt, lt
  Comparator #(.mode("unsigned")) comparator_60 (.a(Prev_byte), .b(8'h46), .eq(comparator_60_eq));  // open: gt, lt
  Comparator #(.mode("unsigned"), .width(4)) comparator_61 (
    .a(Inst[7:4]), .b(4'b0000), .eq(comparator_61_eq));  // open: gt, lt
  and and_50 (Isadd_imm, comparator_50_eq, comparator_51_eq, Is2ndbyte);
  and and_51 (Issub_imm, comparator_52_eq, comparator_53_eq, Is2ndbyte);
  and and_52 (Isand_imm, comparator_54_eq, comparator_55_eq, Is2ndbyte);
  and and_53 (Isxor_imm, comparator_56_eq, comparator_57_eq, Is2ndbyte);
  and and_54 (Isor_imm, comparator_58_eq, comparator_59_eq, Is2ndbyte);
  and and_55 (Isr4_imm, comparator_60_eq, comparator_61_eq, Is2ndbyte);
  Priority_Encoder priority_encoder_4 (
    .in0(Isbnza_a), .in1(Isbnzb_a), .in3(Isbnzd_a), .in5(Isfrom_ioa), .out(priority_encoder_4_out));  // open: in2, in4, in6, in7, en_in, gs, en_out
  Priority_Encoder priority_encoder_5 (
    .in0(Israrb_imm_a), .in1(Israrb_imm_b), .in2(Isrcrd_imm_a), .in3(Isrcrd_imm_b), .in4(Isr4_imm),
    .out(priority_encoder_5_out));  // open: in5, in6, in7, en_in, gs, en_out
  or or_23 (Is11bitimm, Isbbit_kimm_b, Isbnza_b, Isbnzb_b, Isbnzd_b, Isbeqz_b, Isbnez_b, Isbeqzcf_b, Isbnezcf_b);
  or or_24 (Is12bitimm, Isb_b, Iscall_b);
  Multiplexer #(.enable("true"), .width(3)) multiplexer_1 (
    .in0(priority_encoder_4_out), .in1(Inst[3:1]), .out(rs), .sel(IsRRR));  // open: en
  Multiplexer #(.enable("true"), .width(3)) multiplexer_2 (
    .in0(priority_encoder_5_out), .in1(Inst[3:1]), .out(rd), .sel(IsRRR));  // open: en
  // Probe on rs
  // Probe on rd
  Comparator #(.mode("unsigned"), .width(4)) comparator_62 (
    .a(Inst[7:4]), .b(4'b0101), .eq(comparator_62_eq));  // open: gt, lt
  Comparator #(.mode("unsigned"), .width(4)) comparator_63 (
    .a(Prev_byte[7:4]), .b(4'b0101), .eq(comparator_63_eq));  // open: gt, lt
  Comparator #(.mode("unsigned"), .width(4)) comparator_64 (
    .a(Inst[7:4]), .b(4'b0110), .eq(comparator_64_eq));  // open: gt, lt
  Comparator #(.mode("unsigned"), .width(4)) comparator_65 (
    .a(Prev_byte[7:4]), .b(4'b0110), .eq(comparator_65_eq));  // open: gt, lt
  Comparator #(.mode("unsigned"), .width(3)) comparator_66 (
    .a(Inst[7:5]), .b(3'b100), .eq(comparator_66_eq));  // open: gt, lt
  Comparator #(.mode("unsigned"), .width(3)) comparator_67 (
    .a(Prev_byte[7:5]), .b(3'b100), .eq(comparator_67_eq));  // open: gt, lt
  Comparator #(.mode("unsigned"), .width(5)) comparator_68 (
    .a(Inst[7:3]), .b(5'b10100), .eq(comparator_68_eq));  // open: gt, lt
  Comparator #(.mode("unsigned"), .width(5)) comparator_69 (
    .a(Prev_byte[7:3]), .b(5'b10100), .eq(comparator_69_eq));  // open: gt, lt
  and and_56 (Israrb_imm_a, comparator_62_eq, Is2byte);
  and and_57 (Israrb_imm_b, comparator_63_eq, Is2ndbyte);
  and and_58 (Isrcrd_imm_a, comparator_64_eq, Is2byte);
  and and_59 (Isrcrd_imm_b, comparator_65_eq, Is2ndbyte);
  and and_60 (Isbbit_kimm_a, comparator_66_eq, Is2byte);
  and and_61 (Isbbit_kimm_b, comparator_67_eq, Is2ndbyte);
  and and_62 (Isbnza_a, comparator_68_eq, Is2byte);
  and and_63 (Isbnza_b, comparator_69_eq, Is2ndbyte);
  Priority_Encoder priority_encoder_6 (
    .in0(Is4bitimm), .in1(Is2bitimm), .in2(Is11bitimm), .in3(Is12bitimm), .out(ImmSrc));  // open: in4, in5, in6, in7, en_in, gs, en_out
  Comparator #(.mode("unsigned"), .width(5)) comparator_70 (
    .a(Inst[7:3]), .b(5'b10101), .eq(comparator_70_eq));  // open: gt, lt
  Comparator #(.mode("unsigned"), .width(5)) comparator_71 (
    .a(Prev_byte[7:3]), .b(5'b10101), .eq(comparator_71_eq));  // open: gt, lt
  Comparator #(.mode("unsigned"), .width(5)) comparator_72 (
    .a(Inst[7:3]), .b(5'b10110), .eq(comparator_72_eq));  // open: gt, lt
  Comparator #(.mode("unsigned"), .width(5)) comparator_73 (
    .a(Prev_byte[7:3]), .b(5'b10110), .eq(comparator_73_eq));  // open: gt, lt
  Comparator #(.mode("unsigned"), .width(5)) comparator_74 (
    .a(Inst[7:3]), .b(5'b10111), .eq(comparator_74_eq));  // open: gt, lt
  Comparator #(.mode("unsigned"), .width(5)) comparator_75 (
    .a(Prev_byte[7:3]), .b(5'b10111), .eq(comparator_75_eq));  // open: gt, lt
  Comparator #(.mode("unsigned"), .width(5)) comparator_76 (
    .a(Inst[7:3]), .b(5'b11000), .eq(comparator_76_eq));  // open: gt, lt
  Comparator #(.mode("unsigned"), .width(5)) comparator_77 (
    .a(Prev_byte[7:3]), .b(5'b11000), .eq(comparator_77_eq));  // open: gt, lt
  Comparator #(.mode("unsigned"), .width(5)) comparator_78 (
    .a(Inst[7:3]), .b(5'b11001), .eq(comparator_78_eq));  // open: gt, lt
  Comparator #(.mode("unsigned"), .width(5)) comparator_79 (
    .a(Prev_byte[7:3]), .b(5'b11001), .eq(comparator_79_eq));  // open: gt, lt
  and and_64 (Isbnzb_a, comparator_70_eq, Is2byte);
  and and_65 (Isbnzb_b, comparator_71_eq, Is2ndbyte);
  and and_66 (Isbeqz_a, comparator_72_eq, Is2byte);
  and and_67 (Isbeqz_b, comparator_73_eq, Is2ndbyte);
  and and_68 (Isbnez_a, comparator_74_eq, Is2byte);
  and and_69 (Isbnez_b, comparator_75_eq, Is2ndbyte);
  and and_70 (Isbeqzcf_a, comparator_76_eq, Is2byte);
  and and_71 (Isbeqzcf_b, comparator_77_eq, Is2ndbyte);
  and and_72 (Isbnezcf_a, comparator_78_eq, Is2byte);
  and and_73 (Isbnezcf_b, comparator_79_eq, Is2ndbyte);
  Comparator #(.mode("unsigned"), .width(5)) comparator_80 (
    .a(Inst[7:3]), .b(5'b11011), .eq(comparator_80_eq));  // open: gt, lt
  Comparator #(.mode("unsigned"), .width(5)) comparator_81 (
    .a(Prev_byte[7:3]), .b(5'b11011), .eq(comparator_81_eq));  // open: gt, lt
  Comparator #(.mode("unsigned"), .width(4)) comparator_82 (
    .a(Inst[7:4]), .b(4'b1110), .eq(comparator_82_eq));  // open: gt, lt
  Comparator #(.mode("unsigned"), .width(4)) comparator_83 (
    .a(Prev_byte[7:4]), .b(4'b1110), .eq(comparator_83_eq));  // open: gt, lt
  Comparator #(.mode("unsigned"), .width(4)) comparator_84 (
    .a(Inst[7:4]), .b(4'b1111), .eq(comparator_84_eq));  // open: gt, lt
  Comparator #(.mode("unsigned"), .width(4)) comparator_85 (
    .a(Prev_byte[7:4]), .b(4'b1111), .eq(comparator_85_eq));  // open: gt, lt
  and and_74 (Isbnzd_a, comparator_80_eq, Is2byte);
  and and_75 (Isbnzd_b, comparator_81_eq, Is2ndbyte);
  and and_76 (Isb_a, comparator_82_eq, Is2byte);
  and and_77 (Isb_b, comparator_83_eq, Is2ndbyte);
  and and_78 (Iscall_a, comparator_84_eq, Is2byte);
  and and_79 (Iscall_b, comparator_85_eq, Is2ndbyte);
  not not_42 (Power, IsShutdown_B);
  nor nor_1 (Is2byte, Is1byte, Is2ndbyte);

  // Other names for the same wires on the sheet: firstbit = Inst[0]; RRR[2:0] = Inst[3:1]; opcode[3:0] = Inst[7:4];
  //   IsRDRC = ConcatSrc; Prev_opcode[3:0] = Prev_byte[7:4]

  // Notes on the sheet:
  //   Input
  //   Helpers
  //   1 byte instructions
  //   Control Signals
  //   isACC
  //   2 byte instructions
  //   Output
endmodule

module ConcatInator (
  input  [3:0] Arg1,
  input  [3:0] Arg2,
  output [7:0] concat
);


  assign concat = {Arg1, Arg2};
endmodule

module PCTargethandler (
  input  [15:0] TEMPData,
  input  [15:0] PCIn,
  input  [1:0] PCTargetControl,
  input  [15:0] Imm,
  output [15:0] PCTarget,
  output [15:0] TEMPOut
);

  wire [15:0] adder_1_out;

  // Probe on PCIn[4:0]
  // Probe on Imm[10:0]
  Adder #(.width(16)) adder_1 (.a(PCIn), .b(16'h2), .out(adder_1_out));  // open: cin, cout
  Multiplexer #(.enable("true"), .select(2), .width(16)) multiplexer_1 (
    .in0({TEMPData[15:4], PCIn[3:0]}), .in1({Imm[10:0], PCIn[4:0]}), .in2({Imm[11:0], PCIn[3:0]}),
    .out(PCTarget), .sel(PCTargetControl));  // open: in3, en
  Multiplexer #(.enable("true"), .select(2), .width(16)) multiplexer_2 (
    .in0({16{1'b0}}), .in1(TEMPData), .in2(adder_1_out), .out(TEMPOut), .sel(PCTargetControl));  // open: in3, en
  // Probe on PCTarget

  // Other names for the same wires on the sheet: TEMP[15:0] = TEMPData; NewPC[15:0] = PCTarget;
  //   NewTEMP[15:0] = TEMPOut

  // Notes on the sheet:
  //   Set last 12 bits of PC to last 12 bits of TEMP; keep first four bits of PC; set TEMP to 0 (uses PCTarget?)
endmodule
